# Fritzing sketch wiring (saved by Fritzing 0.8.7b)

parts:
  Part1 = Arduino Mega 2560 (Rev3)
  LED1 = LED - 5mm [color="Red (633nm)" package="5 mm [THT]"]
  S1 = Toggle Switch [package=THT]
  U1 = MIDI_CONN_FEMALE [package=din_5_female]  # not connected
  R1 = Resistor [package="2010 [SMD]"]
  LED2 = LED - 5mm [color="Red (633nm)" package="5 mm [THT]"]
  S2 = Toggle Switch [package=THT]
  R2 = Resistor [package="2010 [SMD]"]
  R3 = Resistor [package="2010 [SMD]"]
  R4 = Resistor [package="2010 [SMD]"]

nets:
  N1: Part1.D1_TX0, R3.Pin_0
  N2: Part1.D3_PWM, S1.L1
  N3: Part1.D4_PWM, S2.L1
  N4: Part1.5V, R1.Pin_1
  N5: Part1.GND, S1.COM
  N6: LED1.cathode, S1.L2
  N7: LED2.cathode, S2.L2
  N8: R2.Pin_1, R4.Pin_0
